# Fritzing sketch RFID_PC_RP2040Zero (saved by Fritzing 0.9.10b)
breadboards: 1

parts:
  A1 = Waveshare rp2040-zero tht [package=THT]
  Part1 = RFID-RC522-v3
  part = Resistor [tolerance=±5% power=0.25 resistance=220 package=THT]
  R2 = Resistor [tolerance=±5% power=0.25 resistance=220 package=THT]
  part_2 = Resistor [tolerance=±5% resistance=10k package="0603 [SMD]"]
  R1 = Resistor [tolerance=±5% power=0.25 resistance=220 package=THT]
  J1 = Piezo Speaker
  LED1 = RGB LED (com. cathode, rbg) [package="5 mm [THT]"]

nets (from the breadboard view):
  N1: A1.Pin_1, LED1.common_cathode
  N2: A1.Pin_2, Part1.GND, J1.pin1
  N3: A1.Pin_3, Part1.3.3V
  N4: A1.Pin_9, part_2.Pin_1
  N5: A1.Pin_15, Part1.RST
  N6: A1.Pin_16, Part1.MOSI
  N7: A1.Pin_17, Part1.SCK
  N8: A1.Pin_18, Part1.SDA
  N9: A1.Pin_19, Part1.MISO
  N10: A1.Pin_21, part.Pin_1
  N11: A1.Pin_22, R2.Pin_1
  N12: A1.Pin_23, R1.Pin_1
  N13: part.Pin_0, LED1.green_anode
  N14: R2.Pin_0, LED1.blue_anode
  N15: part_2.Pin_0, J1.pin2
  N16: R1.Pin_0, LED1.red_anode

notes:
  0-LED Blue
  1-LED Green
  2-LED Red
  14-Buzzer
  RFID-RC522
  8-RST
  7-MOSI
  6-SCK
  5-SDA (CS)
  4-MISO

custom parts:
  Waveshare rp2040-zero tht: .RP2040-Zero, A Low-Cost, High-Performance Pico-Like MCU Board Based On Raspberry Pi Microcontroller RP2040. This varant is THT without the extra connections.
  RFID-RC522-v3: A simple China made RFID-RC522 Reader (6x4 cm); do check the pin labels, as this is a MFRC522 based clone.
